# Fritzing sketch auto-pumpkin (saved by Fritzing 0.9.2b)
breadboards: 1

parts:
  Part1 = Arduino Nano (Rev3.0)
  PIR1 = PIR sensor
  Part2 = Breakout Board for Electret Microphone
  Part3 = LC Studio SD Card Module

nets:
  GND: Part1.GND, PIR1.GND, Part2.GND, Part3.GND
  N1: Part1.D4, Part3.CS
  N2: Part1.D7, PIR1.SIG
  N3: Part1.D11/MOSI, Part3.MOSI
  N4: Part1.D12/MISO, Part3.MISO
  5V: Part1.5V, PIR1.VDD, Part3.5V
  N5: Part1.A2, Part2.AUD
  3V3: Part1.3V3, Part2.VCC
  N6: Part1.D13/SCK, Part3.SCK

custom parts:
  LC Studio SD Card Module: The LC Studio SD card module serves as an interface to an SD card. The module works at 3.3 volts and 5 volts. The SPI (Serial Peripheral Interface) protocol is used for communicating with the module.
